# Fritzing sketch circuit_layout (saved by Fritzing 0.7.12b)
breadboards: 1

parts:
  RaspberryPi = Raspberry Pi Model B
  3_PIN_FAN = male pin header, 3 pins [form="♂ (male)"]
  Q1 = NPN-Transistor [package="TO92 [THT]"]
  R1 = Resistor [tolerance=±5% resistance=220 package=THT]

nets:
  N1: RaspberryPi.5V, 3_PIN_FAN.pin2
  N2: RaspberryPi.GND, Q1.C
  N3: RaspberryPi.#17, 3_PIN_FAN.pin1
  N4: RaspberryPi.#18, R1.Pin_0
  N5: 3_PIN_FAN.pin3, Q1.E
  N6: Q1.B, R1.Pin_1

notes:
  3 PIN 5V Fan

custom parts:
  Raspberry Pi Model B: Raspberry Pi (Model B)
